# Fritzing sketch Semaforo (saved by Fritzing 0.9.3b)
breadboards: 1

parts:
  LED1 = LED - 3mm [color="Green (555nm)" package="3 mm [THT]"]
  LED2 = LED - 3mm [color="Orange (620nm)" package="3 mm [THT]"]
  LED3 = LED - 3mm [color="Red (633nm)" package="3 mm [THT]"]
  Componente1 = Arduino Uno (Rev3) - ICSP

nets:
  N1: LED1.cathode, Componente1.D11_PWM/MOSI
  N2: LED1.anode, LED2.anode, LED3.anode, Componente1.GND
  N3: LED2.cathode, Componente1.D12/MISO
  N4: LED3.cathode, Componente1.D13/SCK

// code stored in the sketch: Codigo1.ino
//METODO QUE CONFIGURA EL ARDUINO ANTES DE INIICIAR EL CICLO LOOP
void setup() {
  //EL METODO PINMODE LE DICE AL ARDUINO QUE PREPARE UN PUERTO COMO ENTRADA O SALIDA
  pinMode(11, OUTPUT);//VERDE
  pinMode(12, OUTPUT);//AMARILLO/NARANJA
  pinMode(13, OUTPUT);//ROJO
}
//METODO QUE SE REPITE INDEFINIDAMENTE HASTA QUE EL DISPOSITIVO SE APAGUE
void loop() {
	//LUZ ROJA ENCENDIDA
  digitalWrite(13,HIGH);
	//ESPERA DE 3 SEGUNDOS
  delay(3000);
	//LUZ ROJA APAGADA
  digitalWrite(13,LOW);
  //////////////////////////CAMBIO DE LUZ///////////////////////
	//LUZ AMARILLA/NARANJA ENCENDIDA
  digitalWrite(12,HIGH);
	//ESPERA DE 3 SEGUNDOS
  delay(3000);
	//LUZ AMARILLA/NARANJA APAGADA
  digitalWrite(12,LOW);
  //////////////////////////CAMBIO DE LUZ///////////////////////
	//LUZ VERDE ENCENDIDA
  digitalWrite(11,HIGH);
	//ESPERA DE 3 SEGUNDOS
  delay(3000);
	//LUZ VERDE APAGADA
  digitalWrite(11,LOW);
  //////////////////////////CAMBIO DE LUZ///////////////////////
}
